// Logisim project SynthBite16.circ as structural Verilog: 1 circuit, main circuit SynthBite16
// Micro-Instruction number
module SynthBite16 (
  input  [15:0] in_1
);

  wire AC_p2, AC_p3, AC_p18, AC_p19, AC_p20, AC_p21, AC_p22, AC_p23, AC_p24, AC_p25, AC_p26, AC_p27, AC_p28,
       AC_p29, adder_3_cout, adder_4_cout, and_1_out, and_2_out, and_3_out, and_4_out, and_6_out, and_8_out,
       and_11_out, and_12_out, and_13_out, and_14_out, and_15_out, button_1_out, button_2_out, carry_q,
       comparator_1_eq, comparator_1_gt, comparator_1_lt, d_ff_1_q, d_ff_2_q, d_ff_3_q, decoder_1_out0,
       decoder_1_out1, decoder_1_out2, decoder_1_out3, decoder_1_out4, decoder_1_out5, decoder_1_out6,
       decoder_1_out7, decoder_1_out10, decoder_1_out11, decoder_1_out12, decoder_2_out0, decoder_2_out1,
       decoder_2_out3, decoder_2_out4, decoder_2_out5, decoder_2_out6, decoder_2_out10, decoder_2_out11,
       decoder_2_out12, decoder_2_out13, decoder_2_out14, decoder_2_out15, demultiplexer_1_out0,
       demultiplexer_1_out1, demultiplexer_1_out2, demultiplexer_1_out3, demultiplexer_1_out4,
       demultiplexer_1_out5, demultiplexer_1_out6, demultiplexer_1_out7, IE_q, keyboard_1_avail,
       keyboard_2_avail, mAC_p2, MasterClock_out, multiplexer_10_out, nand_1_out, not_1_out, not_2_out,
       not_3_out, not_4_out, not_5_out, not_6_out, not_8_out, not_10_out, or_1_out, or_2_out, or_4_out,
       or_6_out, or_7_out, or_8_out, PC_carry, register_9_q, register_10_q, register_11_q, register_12_q,
       SP_carry, timing_sig_carry, undriven_3, undriven_4, undriven_5;
  wire [0:0] DR_q, not_9_out;
  wire [2:0] SP_q;
  wire [3:0] multiplexer_5_out;
  wire [5:4] multiplexer_6_out;
  wire [6:0] keyboard_1_data, keyboard_2_data, outr_q_2, rand_q;
  wire [7:0] CAR_q, lookup_control_mem_address_for_instruction_data, multiplexer_4_out, rand_q_3;
  wire [7:7] rand_q_2;
  wire [11:0] adder_1_out, AR_q, controlled_buffer_4_out, multiplexer_3_out, PC_q;
  wire [15:0] adder_2_out, adder_3_out, adder_4_out, adder_5_out, and_5_out, and_9_out, and_10_out,
       controlled_buffer_1_out, CWR_q, dAC_p18, DR_q_2, IR_q, mAC_p1, mAC_p4, multiplexer_1_out,
       multiplexer_2_out, multiplexer_7_out, multiplexer_8_out, multiplexer_9_out, not_7_out, or_3_out,
       register_1_q, register_2_q, register_3_q, register_4_q, register_5_q, register_6_q, register_7_q,
       register_8_q, subtractor_1_out, subtractor_2_out, TR_q, undriven_2, xnor_1_out, xnor_2_out,
       xnor_3_out, xor_1_out;
  wire [15:7] outr_q;
  wire [15:15] undriven;
  wire [31:0] CNTRL_MEM_data;

  LED led_1 (.in(MasterClock_out));
  Clock MasterClock (.out(MasterClock_out));
  Keyboard keyboard_1 (
    .clk(MasterClock_out), .re(1'b1), .clr(CWR_q[1]), .avail(keyboard_1_avail), .data(keyboard_1_data));
  Counter #(.max('h7), .trigger("falling"), .width(3)) SP (
    .clr(button_1_out), .up(CWR_q[9]), .count(CWR_q[10]), .clk(MasterClock_out), .carry(SP_carry), .Q(SP_q));  // open: load, D
  and and_1 (and_1_out, MasterClock_out, CWR_q[7]);
  assign controlled_buffer_1_out = or_7_out ? {4'b0000, IR_q[11:0]} : 16'bz;  // Controlled_Buffer controlled_buffer_1
  assign controlled_buffer_1_out = decoder_1_out7 ? {4'b0000, PC_q} : 16'bz;  // Controlled_Buffer controlled_buffer_2
  assign controlled_buffer_1_out = decoder_1_out12 ? multiplexer_1_out : 16'bz;  // Controlled_Buffer controlled_buffer_3
  Multiplexer #(.select(3), .width(16)) multiplexer_1 (
    .in0(register_1_q), .in1(register_2_q), .in2(register_3_q), .in3(register_4_q), .in4(register_5_q),
    .in5(register_6_q), .in6(register_7_q), .in7(register_8_q), .out(multiplexer_1_out), .sel(SP_q));
  assign controlled_buffer_4_out = and_1_out ? AR_q : 12'bz;  // Controlled_Buffer controlled_buffer_4
  Register #(.trigger("falling"), .width(12)) AR (
    .D(controlled_buffer_1_out[11:0]), .en(decoder_2_out5), .clk(MasterClock_out), .Q(AR_q),
    .clr(button_1_out));
  LedBar #(.matrixcols(4)) ledbar_1 (
    .led0(controlled_buffer_1_out[15]), .led1(controlled_buffer_1_out[14]),
    .led2(controlled_buffer_1_out[13]), .led3(controlled_buffer_1_out[12]));
  Counter #(.max('hfff), .trigger("falling"), .width(12)) PC (
    .clr(button_1_out), .load(decoder_2_out3), .up(1'b1), .count(CWR_q[0]), .clk(MasterClock_out),
    .D(adder_1_out), .carry(PC_carry), .Q(PC_q));
  Demultiplexer #(.enable("true"), .select(3)) demultiplexer_1 (
    .out0(demultiplexer_1_out0), .out1(demultiplexer_1_out1), .out2(demultiplexer_1_out2),
    .out3(demultiplexer_1_out3), .out4(demultiplexer_1_out4), .out5(demultiplexer_1_out5),
    .out6(demultiplexer_1_out6), .out7(demultiplexer_1_out7), .in(1'b1), .sel(SP_q), .en(decoder_2_out15));
  Register #(.trigger("falling"), .width(16)) TR (
    .D(controlled_buffer_1_out), .en(decoder_2_out6), .clk(MasterClock_out), .Q(TR_q), .clr(button_1_out));
  assign controlled_buffer_1_out = decoder_1_out6 ? TR_q : 16'bz;  // Controlled_Buffer controlled_buffer_5
  Register #(.trigger("falling"), .width(16)) DR (
    .D(controlled_buffer_1_out), .en(decoder_2_out10), .clk(MasterClock_out), .Q({DR_q_2[14:0], DR_q[0]}),
    .clr(button_1_out));
  assign controlled_buffer_1_out = and_2_out ? {DR_q_2[14:0], DR_q[0]} : 16'bz;  // Controlled_Buffer controlled_buffer_6
  Multiplexer #(.width(16)) multiplexer_2 (
    .in0({16{1'b1}}), .in1({{9{1'b0}}, keyboard_1_data}), .out(multiplexer_2_out), .sel(keyboard_1_avail));
  assign controlled_buffer_1_out = decoder_1_out5 ? multiplexer_2_out : 16'bz;  // Controlled_Buffer controlled_buffer_7
  // Probe on PC_q
  D_Flip_Flop #(.trigger("falling")) d_ff_1 (
    .D(CWR_q[0]), .clk(MasterClock_out), .Q(d_ff_1_q), .preset(button_1_out));  // open: Qn, reset
  DotMatrix #(.matrixcols(4), .matrixrows(1)) dotmatrix_1 (
    .col0(SP_carry), .col1(SP_carry), .col2(SP_carry), .col3(SP_carry));
  Register #(.trigger("falling"), .width(16)) register_1 (
    .D(controlled_buffer_1_out), .en(demultiplexer_1_out0), .clk(MasterClock_out), .Q(register_1_q),
    .clr(button_1_out));
  Register #(.trigger("falling"), .width(16)) register_2 (
    .D(controlled_buffer_1_out), .en(demultiplexer_1_out1), .clk(MasterClock_out), .Q(register_2_q),
    .clr(button_1_out));
  and and_2 (and_2_out, decoder_1_out3, MasterClock_out);
  Multiplexer #(.width(12)) multiplexer_3 (
    .in0(controlled_buffer_4_out), .in1(PC_q), .out(multiplexer_3_out), .sel(and_3_out));
  Register #(.trigger("falling"), .width(16)) register_3 (
    .D(controlled_buffer_1_out), .en(demultiplexer_1_out2), .clk(MasterClock_out), .Q(register_3_q),
    .clr(button_1_out));
  Register #(.trigger("falling"), .width(16)) register_4 (
    .D(controlled_buffer_1_out), .en(demultiplexer_1_out3), .clk(MasterClock_out), .Q(register_4_q),
    .clr(button_1_out));
  or or_1 (or_1_out, CWR_q[6], d_ff_1_q);
  assign controlled_buffer_4_out = or_1_out ? PC_q : 12'bz;  // Controlled_Buffer controlled_buffer_8
  and and_3 (and_3_out, IR_q[12], IR_q[13], not_1_out, not_2_out);
  Register #(.trigger("falling"), .width(16)) register_5 (
    .D(controlled_buffer_1_out), .en(demultiplexer_1_out4), .clk(MasterClock_out), .Q(register_5_q),
    .clr(button_1_out));
  Register #(.trigger("falling"), .width(16)) register_6 (
    .D(controlled_buffer_1_out), .en(demultiplexer_1_out5), .clk(MasterClock_out), .Q(register_6_q),
    .clr(button_1_out));
  Register #(.trigger("falling"), .width(16)) register_7 (
    .D(controlled_buffer_1_out), .en(demultiplexer_1_out6), .clk(MasterClock_out), .Q(register_7_q),
    .clr(button_1_out));
  Register #(.trigger("falling"), .width(16)) register_8 (
    .D(controlled_buffer_1_out), .en(demultiplexer_1_out7), .clk(MasterClock_out), .Q(register_8_q),
    .clr(button_1_out));
  Counter timing_sig (
    .clr(button_1_out), .up(1'b1), .count(1'b1), .clk(CWR_q[0]), .carry(timing_sig_carry));  // open: load, D, Q
  Adder #(.width(12)) adder_1 (.a(multiplexer_3_out), .b(12'h1), .out(adder_1_out));  // open: cin, cout
  not not_1 (not_1_out, IR_q[14]);
  not not_2 (not_2_out, register_12_q);
  LED led_2 (.in(PC_carry));
  not not_3 (not_3_out, d_ff_1_q);
  and and_4 (and_4_out, CWR_q[8], not_3_out);
  assign controlled_buffer_4_out = and_4_out ? IR_q[11:0] : 12'bz;  // Controlled_Buffer controlled_buffer_9
  Button button_1 (.out(button_1_out));
  LedBar #(.matrixcols(16)) ledbar_2 (
    .led0(IR_q[15]), .led1(IR_q[14]), .led2(IR_q[13]), .led3(IR_q[12]), .led4(IR_q[11]), .led5(IR_q[10]),
    .led6(IR_q[9]), .led7(IR_q[8]), .led8(IR_q[7]), .led9(IR_q[6]), .led10(IR_q[5]), .led11(IR_q[4]),
    .led12(IR_q[3]), .led13(IR_q[2]), .led14(IR_q[1]), .led15(IR_q[0]));
  or or_2 (or_2_out, d_ff_1_q, decoder_2_out11);
  // Probe on timing_sig_carry
  TTY tty_1 (.data(rand_q), .clk(MasterClock_out), .we(1'b1), .clr(button_2_out));
  Adder #(.width(16)) adder_2 (
    .a({rand_q_3, rand_q_2[7], rand_q}), .b(mAC_p4), .out(adder_2_out), .cin(MasterClock_out));  // open: cout
  assign and_5_out = CWR_q & {rand_q_3, rand_q_2[7], rand_q};  // AND_Gate and_5, 16 bits wide
  Register #(.width(16)) IR (
    .D(controlled_buffer_1_out), .en(or_2_out), .clk(MasterClock_out), .Q(IR_q), .clr(button_1_out));
  Adder #(.width(16)) adder_3 (
    .a({DR_q_2[14:0], DR_q[0]}), .b(controlled_buffer_1_out), .out(adder_3_out), .cin(DR_q_2[15]),
    .cout(adder_3_cout));
  assign xnor_1_out = ~(adder_2_out ^ {rand_q_3, rand_q_2[7], rand_q});  // XNOR_Gate xnor_1, 16 bits wide
  assign xnor_2_out = ~(xnor_1_out ^ and_5_out);  // XNOR_Gate xnor_2, 16 bits wide
  not not_4 (not_4_out, IR_q[14]);
  not not_5 (not_5_out, IR_q[13]);
  Subtractor #(.width(16)) subtractor_1 (
    .a({DR_q_2[14:0], DR_q[0]}), .b(controlled_buffer_1_out), .out(subtractor_1_out), .bin(DR_q_2[15]));  // open: bout
  assign or_3_out = controlled_buffer_1_out | {DR_q_2[14:0], DR_q[0]};  // OR_Gate or_3, 16 bits wide
  TTY tty_2 (.data(outr_q_2), .clk(MasterClock_out), .we(decoder_2_out12), .clr(button_2_out));
  and and_6 (and_6_out, not_4_out, not_5_out);
  not not_6 (not_6_out, IR_q[12]);
  // Probe on controlled_buffer_1_out
  // Probe on controlled_buffer_4_out
  assign not_7_out = ~{DR_q_2[14:0], DR_q[0]};  // NOT_Gate not_7, 16 bits wide
  Register #(.width(16)) \rand  (
    .D(xnor_3_out), .en(1'b1), .clk(MasterClock_out), .Q({rand_q_3, rand_q_2[7], rand_q}), .clr(button_1_out));
  assign xnor_3_out = ~(xnor_2_out ^ {rand_q_3, rand_q_2[7], rand_q});  // XNOR_Gate xnor_3, 16 bits wide
  and and_7 (multiplexer_6_out[5], and_6_out, not_6_out);
  Multiplexer #(.width(8)) multiplexer_4 (
    .in0(lookup_control_mem_address_for_instruction_data), .in1(8'hf9), .out(multiplexer_4_out),
    .sel(and_8_out));
  or or_4 (or_4_out, adder_3_cout, adder_4_cout, DR_q[0]);
  assign xor_1_out = controlled_buffer_1_out ^ {DR_q_2[14:0], DR_q[0]};  // XOR_Gate xor_1, 16 bits wide
  and and_8 (and_8_out, keyboard_2_avail, IE_q);
  assign and_9_out = controlled_buffer_1_out & {DR_q_2[14:0], DR_q[0]};  // AND_Gate and_9, 16 bits wide
  assign and_10_out = {DR_q_2[14:0], DR_q[0]} & {16{undriven[15]}};  // AND_Gate and_10, 16 bits wide
  Adder #(.width(16)) adder_4 (.a(mAC_p1), .b(and_10_out), .out(adder_4_out), .cin(1'b0), .cout(adder_4_cout));
  Button button_2 (.out(button_2_out));
  Multiplexer #(.width(4)) multiplexer_5 (
    .in0(IR_q[15:12]), .in1(IR_q[11:8]), .out(multiplexer_5_out), .sel(multiplexer_6_out[5]));
  // Probe on keyboard_2_data
  // Shift_Register #(.length(16), .trigger("falling")) mAC: pin names not known; wires that end beside it: mAC_p1, mAC_p2, mAC_p4[1], mAC_p4[0], MasterClock_out, 1'b0
  Register #(.trigger("falling"), .width(16)) outr (
    .D(controlled_buffer_1_out), .en(decoder_2_out12), .clk(MasterClock_out), .Q({outr_q, outr_q_2}),
    .clr(button_1_out));
  Multiplexer multiplexer_6 (.in0(1'b0), .in1(IR_q[15]), .out(multiplexer_6_out[4]), .sel(multiplexer_6_out[5]));
  D_Flip_Flop d_ff_2 (.clk(MasterClock_out), .Q(d_ff_2_q), .preset(d_ff_3_q), .reset(button_1_out));  // open: D, Qn
  D_Flip_Flop d_ff_3 (.D(d_ff_1_q), .clk(MasterClock_out), .Q(d_ff_3_q), .reset(button_1_out));  // open: Qn, preset
  Register #(.trigger("falling"), .width(1)) IE (
    .D(CWR_q[4]), .en(CWR_q[5]), .clk(MasterClock_out), .Q(IE_q), .clr(button_1_out));
  Adder #(.width(16)) adder_5 (.a(16'h1), .b(controlled_buffer_1_out), .out(adder_5_out));  // open: cin, cout
  and and_11 (and_11_out, d_ff_2_q, d_ff_3_q);
  // Probe on mAC_p1
  Hex_Digit_Display #(.decimalPoint("false")) hex_digit_display_1 (.value(outr_q[15:12]));
  Hex_Digit_Display #(.decimalPoint("false")) hex_digit_display_2 (.value(outr_q[11:8]));
  ROM #(.addrWidth(6)) lookup_control_mem_address_for_instruction (
    .addr({multiplexer_6_out, multiplexer_5_out}), .data(lookup_control_mem_address_for_instruction_data));
  not not_8 (not_8_out, d_ff_3_q);
  Comparator #(.width(16)) comparator_1 (
    .a(controlled_buffer_1_out), .b({DR_q_2[14:0], DR_q[0]}), .gt(comparator_1_gt), .eq(comparator_1_eq),
    .lt(comparator_1_lt));
  Subtractor #(.width(16)) subtractor_2 (
    .a(dAC_p18), .b({DR_q_2[14:0], DR_q[0]}), .out(subtractor_2_out));  // open: bin, bout
  Hex_Digit_Display #(.decimalPoint("false")) hex_digit_display_3 (.value({outr_q[7], outr_q_2[6:4]}));
  Counter #(.trigger("falling")) CAR (
    .clr(button_1_out), .load(and_11_out), .up(1'b1), .clk(MasterClock_out), .D(multiplexer_4_out), .Q(CAR_q));  // open: count, carry
  or or_5 (mAC_p2, CWR_q[12], button_1_out);
  Multiplexer #(.width(16)) multiplexer_7 (
    .in0(subtractor_2_out), .in1(controlled_buffer_1_out), .out(multiplexer_7_out), .sel(and_12_out));
  assign controlled_buffer_1_out = decoder_1_out10 ? dAC_p18 : 16'bz;  // Controlled_Buffer controlled_buffer_10
  Hex_Digit_Display #(.decimalPoint("false")) hex_digit_display_4 (.value(outr_q_2[3:0]));
  and and_12 (and_12_out, CWR_q[11], undriven_2[15], mAC_p4[1]);
  // Shift_Register #(.length(16), .trigger("falling")) dAC: pin names not known; wires that end beside it: mAC_p2, mAC_p4[1], mAC_p4[0], MasterClock_out, undriven_2[15], multiplexer_7_out[0], multiplexer_7_out[1], multiplexer_7_out[2], multiplexer_7_out[3], multiplexer_7_out[4], multiplexer_7_out[5], multiplexer_7_out[6], multiplexer_7_out[7], multiplexer_7_out[8], multiplexer_7_out[9], multiplexer_7_out[10], multiplexer_7_out[11], dAC_p18[0], dAC_p18[1], dAC_p18[2], dAC_p18[3], dAC_p18[4], dAC_p18[5], dAC_p18[6], dAC_p18[7], dAC_p18[8], dAC_p18[9], dAC_p18[10], dAC_p18[11]
  ROM #(.dataWidth(32)) CNTRL_MEM (.addr(CAR_q), .data(CNTRL_MEM_data));
  Keyboard #(.buflen(7)) keyboard_2 (
    .clk(MasterClock_out), .re(1'b1), .clr(CWR_q[2]), .avail(keyboard_2_avail), .data(keyboard_2_data));
  not not_9 (not_9_out[0], dAC_p18[15]);
  Multiplexer #(.width(16)) multiplexer_8 (
    .in0({undriven_2[15:1], not_9_out[0]}), .in1(controlled_buffer_1_out), .out(multiplexer_8_out),
    .sel(decoder_2_out14));
  Register #(.width(32)) CWR (
    .D(CNTRL_MEM_data), .en(1'b1), .clk(MasterClock_out), .Q({mAC_p4, CWR_q}), .clr(button_1_out));
  Multiplexer #(.enable("true"), .select(4), .width(16)) multiplexer_9 (
    .in0({DR_q_2[14:0], DR_q[0]}), .in1(not_7_out), .in2(adder_3_out), .in3(subtractor_1_out),
    .in4(or_3_out), .in5(xor_1_out), .in6(and_9_out), .in7(DR_q_2), .in8(in_1),
    .in9({rand_q_3, rand_q_2[7], rand_q}), .in10(adder_5_out), .in11(mAC_p1), .in12(dAC_p18), .in13(in_1),
    .in14(in_1), .in15(in_1), .out(multiplexer_9_out), .sel(mAC_p4[7:4]), .en(mAC_p4[3]));
  // Shift_Register #(.length(16), .trigger("falling")) Q: pin names not known; wires that end beside it: button_1_out, CWR_q[11], mAC_p4[0], MasterClock_out, 1'b0, multiplexer_8_out[0], multiplexer_8_out[1], multiplexer_8_out[2], multiplexer_8_out[3], multiplexer_8_out[4], multiplexer_8_out[5], multiplexer_8_out[6], multiplexer_8_out[7], multiplexer_8_out[8], multiplexer_8_out[9], multiplexer_8_out[10], multiplexer_8_out[11]
  DotMatrix #(.matrixcols(32), .matrixrows(1)) dotmatrix_2 (
    .col0(mAC_p4[15]), .col1(mAC_p4[14]), .col2(mAC_p4[13]), .col3(mAC_p4[12]), .col4(mAC_p4[11]),
    .col5(mAC_p4[10]), .col6(mAC_p4[9]), .col7(mAC_p4[8]), .col8(mAC_p4[7]), .col9(mAC_p4[6]),
    .col10(mAC_p4[5]), .col11(mAC_p4[4]), .col12(mAC_p4[3]), .col13(mAC_p4[2]), .col14(mAC_p4[1]),
    .col15(mAC_p4[0]), .col16(CWR_q[15]), .col17(CWR_q[14]), .col18(CWR_q[13]), .col19(CWR_q[12]),
    .col20(CWR_q[11]), .col21(CWR_q[10]), .col22(CWR_q[9]), .col23(CWR_q[8]), .col24(CWR_q[7]),
    .col25(CWR_q[6]), .col26(CWR_q[5]), .col27(CWR_q[4]), .col28(CWR_q[3]), .col29(CWR_q[2]),
    .col30(CWR_q[1]), .col31(CWR_q[0]));
  // Probe on multiplexer_9_out
  Register #(.trigger("falling"), .width(1)) register_9 (
    .D(comparator_1_lt), .en(decoder_2_out4), .clk(MasterClock_out), .Q(register_9_q), .clr(button_1_out));
  Register #(.trigger("falling"), .width(1)) register_10 (
    .D(comparator_1_eq), .en(decoder_2_out4), .clk(MasterClock_out), .Q(register_10_q), .clr(button_1_out));
  Register #(.trigger("falling"), .width(1)) register_11 (
    .D(comparator_1_gt), .en(decoder_2_out4), .clk(MasterClock_out), .Q(register_11_q), .clr(button_1_out));
  assign controlled_buffer_1_out = decoder_1_out11 ? undriven_2 : 16'bz;  // Controlled_Buffer controlled_buffer_11
  not not_10 (not_10_out, mAC_p4[5]);
  nand nand_1 (nand_1_out, mAC_p4[6], mAC_p4[7]);
  or or_6 (or_6_out, CWR_q[14], CWR_q[15], CWR_q[13]);
  or or_7 (or_7_out, decoder_1_out4, CWR_q[3]);
  and and_13 (and_13_out, not_10_out, nand_1_out);
  or or_8 (or_8_out, d_ff_1_q, decoder_1_out1);
  and and_14 (and_14_out, mAC_p4[4], and_13_out);
  // Shift_Register #(.length(16), .trigger("falling")) AC: pin names not known; wires that end beside it: button_1_out, AC_p2, AC_p3, MasterClock_out, DR_q_2[15], multiplexer_9_out[0], multiplexer_9_out[1], multiplexer_9_out[2], multiplexer_9_out[3], multiplexer_9_out[4], multiplexer_9_out[5], multiplexer_9_out[6], multiplexer_9_out[7], multiplexer_9_out[8], multiplexer_9_out[9], multiplexer_9_out[10], multiplexer_9_out[11], AC_p18, AC_p19, AC_p20, AC_p21, AC_p22, AC_p23, AC_p24, AC_p25, AC_p26, AC_p27, AC_p28, AC_p29
  RAM #(.addrWidth(12), .dataWidth(16), .databus("bidir"), .enables("line"), .trigger("falling")) MEM (
    .addr(controlled_buffer_4_out), .we(decoder_2_out1), .oe(or_8_out), .clk(MasterClock_out),
    .data(controlled_buffer_1_out));
  D_Flip_Flop #(.trigger("falling")) carry (
    .D(or_4_out), .clk(MasterClock_out), .Q(carry_q), .reset(button_1_out));  // open: Qn, preset
  Multiplexer #(.select(3)) multiplexer_10 (
    .in0(1'b0), .in1(1'b1), .in2(carry_q), .in3(register_9_q), .in4(register_10_q), .in5(register_11_q),
    .in6(1'b0), .in7(1'b0), .out(multiplexer_10_out), .sel(CWR_q[15:13]));
  assign controlled_buffer_1_out[0] = and_15_out ? AC_p18 : 1'bz;  // Controlled_Buffer controlled_buffer_12
  assign controlled_buffer_1_out[1] = and_15_out ? AC_p19 : 1'bz;  // Controlled_Buffer controlled_buffer_13
  assign controlled_buffer_1_out[2] = and_15_out ? AC_p20 : 1'bz;  // Controlled_Buffer controlled_buffer_14
  assign controlled_buffer_1_out[3] = and_15_out ? AC_p21 : 1'bz;  // Controlled_Buffer controlled_buffer_15
  assign controlled_buffer_1_out[4] = and_15_out ? AC_p22 : 1'bz;  // Controlled_Buffer controlled_buffer_16
  assign controlled_buffer_1_out[5] = and_15_out ? AC_p23 : 1'bz;  // Controlled_Buffer controlled_buffer_17
  assign controlled_buffer_1_out[6] = and_15_out ? AC_p24 : 1'bz;  // Controlled_Buffer controlled_buffer_18
  assign controlled_buffer_1_out[7] = and_15_out ? AC_p25 : 1'bz;  // Controlled_Buffer controlled_buffer_19
  assign controlled_buffer_1_out[8] = and_15_out ? AC_p26 : 1'bz;  // Controlled_Buffer controlled_buffer_20
  assign controlled_buffer_1_out[9] = and_15_out ? AC_p27 : 1'bz;  // Controlled_Buffer controlled_buffer_21
  assign controlled_buffer_1_out[10] = and_15_out ? AC_p28 : 1'bz;  // Controlled_Buffer controlled_buffer_22
  assign controlled_buffer_1_out[11] = and_15_out ? AC_p29 : 1'bz;  // Controlled_Buffer controlled_buffer_23
  assign controlled_buffer_1_out[12] = and_15_out ? undriven_3 : 1'bz;  // Controlled_Buffer controlled_buffer_24
  assign controlled_buffer_1_out[13] = and_15_out ? undriven_4 : 1'bz;  // Controlled_Buffer controlled_buffer_25
  assign controlled_buffer_1_out[14] = and_15_out ? undriven_5 : 1'bz;  // Controlled_Buffer controlled_buffer_26
  assign controlled_buffer_1_out[15] = and_15_out ? undriven[15] : 1'bz;  // Controlled_Buffer controlled_buffer_27
  LED led_3 (.in(decoder_1_out0));
  Decoder #(.enable("false"), .select(4)) decoder_1 (
    .out0(decoder_1_out0), .out1(decoder_1_out1), .out2(decoder_1_out2), .out3(decoder_1_out3),
    .out4(decoder_1_out4), .out5(decoder_1_out5), .out6(decoder_1_out6), .out7(decoder_1_out7),
    .out10(decoder_1_out10), .out11(decoder_1_out11), .out12(decoder_1_out12), .sel(mAC_p4[15:12]));  // open: out8, out9, out13, out14, out15
  LED led_4 (.in(decoder_2_out0));
  Decoder #(.enable("false"), .select(4)) decoder_2 (
    .out0(decoder_2_out0), .out1(decoder_2_out1), .out2(AC_p2), .out3(decoder_2_out3), .out4(decoder_2_out4),
    .out5(decoder_2_out5), .out6(decoder_2_out6), .out10(decoder_2_out10), .out11(decoder_2_out11),
    .out12(decoder_2_out12), .out13(decoder_2_out13), .out14(decoder_2_out14), .out15(decoder_2_out15),
    .sel(mAC_p4[11:8]));  // open: out7, out8, out9
  Register #(.trigger("falling"), .width(1)) register_12 (
    .D(multiplexer_10_out), .en(or_6_out), .clk(MasterClock_out), .Q(register_12_q), .clr(button_1_out));
  D_Flip_Flop #(.trigger("falling")) d_ff_4 (
    .clk(MasterClock_out), .Q(DR_q_2[15]), .preset(decoder_2_out13), .reset(button_1_out));  // open: D, Qn
  or or_9 (AC_p3, and_14_out, mAC_p4[2]);
  and and_15 (and_15_out, decoder_1_out2, MasterClock_out);

  // Notes on the sheet:
  //   CLOCK
  //   INPUT(BUFFER)
  //   16 LINES
  //   LOAD AN INSTRUCTION
  //   STACK OVERFLOW
  //   REGISTER STACK
  //   ADDRESS BUS
  //   END OF THE LINE
  //   COARSE GRAINED TIMER, DEPENDS ON THE INSTRUCTIONS THAN MICRO-INSTRUCTIONS
  //   COMPUTER REBOOT
  //   ADDRESS BUS
  //   PRESENT INSTRUCTION
  //   AC RESET ASYNC
  //   OP-CODE
  //   RANDOM MESS
  //   ADDRESSING MODE
  //   GENERAL SYSTEM BUS
  //   OUTPUT STREAM
  //   VALUE ON MAIN BUS
  //   VALUE ON ADDRESS BUS
  //   NXT INSN FRM CNTRL MEM OR MEM
  //   ADDRESS BUS
  //   GOTO INTERRUPT ADDRESS(IN CNTROL MEM)
  //   CAR STARTING ADDRESSBUS
  //   INTERRUPT INPUT
  //   SECOND NIBBLE NEEDED?
  //   SYSTEM START EDGE CASE
  //   CONTROL UNIT
  //   ALU
  //   LEAST SIGNIFICANT LINE
  //   ADDRESS BUS
  //   contents of lookup_control_mem_address_for_instruction (hex, n*v repeats v):
  //   0 3 5 7 9 c f 12 0 17 1a 1d 21 24 27 2a 16*0 30 32 34 4a 36 0 46 3c 38 3a 3e 40 48 42 44 0 70 73 75
  //   7c 9a 0 84 87 89 8b 8d 8f 91 94 96 98
  //   MOST SIGNIFICANT LINE
  //   OUTPUT(HEX)
  //   contents of CNTRL_MEM (hex, n*v repeats v):
  //   0 0 0 1a000101 0 21000101 0 13000101 0 71000100 13000101 0 15000100 13000081 0 4a000000 2080001 0
  //   1a000100 21000100 2080001 0 0 15000100 1a000081 0 15000100 21000081 0 15000100 13000081 11*0
  //   15000100 1a000080 21000081 0 0 0 22080001 0 22180001 0 22280001 0 22380001 0 22480001 0 22580001 0
  //   22680001 0 22780001 0 40001 0 22980001 0 22a80001 0 24000001 0 d0000001 0 1000 20020000 50000
  //   20020000 50000 20020000 50000 20020000 50000 20020000 50000 20020000 50000 20020000 50000 20020000
  //   50000 20020000 50000 20020000 50000 20020000 50000 20020000 50000 20020000 50000 20020000 50000
  //   20020000 50000 20020000 2b80001 5*0 600 3f000001 0 401 0 ca000000 20800000 400 ca000000 22280000
  //   2f000001 0 c6000000 400 ca000000 20800000 6a000000 2380000 2f000001 0 ca000000 20800001 0 4001 0
  //   2001 0 6001 0 8001 0 a001 0 5a000000 3 0 2c000001 0 31 0 21 0 ca000400 2080000 ca000000 1000
  //   20020000 50000 20020000 50000 20020000 50000 20020000 50000 20020000 50000 20020000 50000 20020000
  //   50000 20020000 50000 20020000 50000 20020000 50000 20020000 50000 20020000 50000 20020000 50000
  //   20020000 50000 20020000 50000 20020000 2b80000 2f000001 63*0 1b000040
  //   INTERRUPT
  //   ADDRESS BUS
  //   this line is just a place holder
  //   STACK POINTER VALUE MANIPULATE
  //   PRESENT CONTROL
  //   IR(4..=15) ON BUS(ADDRESS)
  //   AR ON BUS(ADDRESS)
  //   PC ON BUS(ADDRESS)
  //   ADDRESS BUS
  //   ACC SHIFT(L)
  //   NONE
  //   ACC ON BUS
  //   DR ON BUS
  //   INPUT ON BUS
  //   TMP ON BUS
  //   PUT ON BUS
  //   dAC ON BUS
  //   Q ON BUS
  //   STACK TOP ON BUS
  //   TMP LOAD
  //   LOAD FROM BUS
  //   DR LOAD
  //   IR LOAD
  //   OUT LOAD
  //   SRL IN
  //   LOAD Q
  //   CONDITION FLIP FLOP
  //   MEM OUT ENABLE
  //   IR ON BUS(GENERAL)
  //   PC ON GENERAL
  //   NONE
  //   MEM WRITE ENABLE
  //   AC PARLLEL LOAD
  //   PC LOAD
  //   LOAD THE COMPARE REG (NOT GENERAL BUS)
  //   AR LOAD
  //   PUSH TO STACK
  //   SERIAL IN
  //   keeping the AC on the bus only for half a cycles to avoid conflicts
endmodule
